// Logisim project Movie_Rating_System.circ as structural Verilog: 1 circuit, main circuit main
module main (
  input  [3:0] User1,
  input  [3:0] User2,
  input  [3:0] User3
);

  wire not_1_out, not_2_out, subtractor_1_bout, subtractor_2_bout;
  wire [3:0] adder_1_out, adder_2_out, bit_extender_1_out, multiplexer_1_out, subtractor_2_out;

  Adder #(.width(4)) adder_1 (.a(User1), .b(User2), .out(adder_1_out));  // open: cin, cout
  Adder #(.width(4)) adder_2 (.a(adder_1_out), .b(User3), .out(adder_2_out));  // open: cin, cout
  Subtractor #(.width(4)) subtractor_1 (.a(adder_2_out), .b(4'b1001), .bout(subtractor_1_bout));  // open: out, bin
  Subtractor #(.width(4)) subtractor_2 (
    .a(adder_2_out), .b(4'b1010), .out(subtractor_2_out), .bout(subtractor_2_bout));  // open: bin
  not not_1 (not_1_out, subtractor_2_bout);
  not not_2 (not_2_out, subtractor_1_bout);
  Multiplexer #(.width(4)) multiplexer_1 (
    .in0(subtractor_2_out), .in1(adder_2_out), .out(multiplexer_1_out), .sel(subtractor_2_bout));
  assign bit_extender_1_out = {{3{1'b0}}, not_1_out};  // Bit_Extender bit_extender_1
  Hex_Digit_Display hex_digit_display_1 (.value(bit_extender_1_out));  // open: dp
  Hex_Digit_Display hex_digit_display_2 (.value(multiplexer_1_out));  // open: dp
  LED Recommended (.in(not_2_out));
endmodule
